// Logisim project cpu.circ as structural Verilog: 1 circuit, main circuit cpu
module cpu (
  input  clk,
  input  [31:0] Instruction,
  input  [31:0] MemReadData,
  output [31:0] MemAddress,
  output [31:0] ProgramCounter,
  output [31:0] ra,
  output [31:0] sp,
  output [31:0] t0,
  output [31:0] t1,
  output [31:0] t2,
  output [31:0] s0,
  output [31:0] s1,
  output [31:0] a0,
  output [3:0] MemWriteMask,
  output [31:0] MemWriteData,
  output [4:0] I_rd,
  output [4:0] I_rs1
);

  wire comparator_2_eq, Imm_I_Type, isAddi;
  wire [4:0] ReadIndex1, WriteIndex;
  wire [31:0] adder_1_out, ALU_A, ALU_B, ALU_RES, Immediate, regfile_1_readdata2;

  Register #(.width(32)) PC (.D(adder_1_out), .clk(clk), .Q(ProgramCounter));  // open: en, clr
  Adder #(.width(32)) adder_1 (.a(ProgramCounter), .b(32'h4), .out(adder_1_out));  // open: cin, cout
  Comparator #(.mode("unsigned"), .width(7)) comparator_1 (
    .a(Instruction[6:0]), .b(7'b0010011), .eq(Imm_I_Type));  // open: gt, lt
  Comparator #(.mode("unsigned"), .width(3)) comparator_2 (
    .a(Instruction[14:12]), .b(3'b000), .eq(comparator_2_eq));  // open: gt, lt
  and and_1 (isAddi, comparator_2_eq, Imm_I_Type);
  Multiplexer #(.width(5)) multiplexer_1 (.in1(Instruction[19:15]), .out(ReadIndex1), .sel(Imm_I_Type));  // open: in0
  Multiplexer #(.width(5)) multiplexer_2 (.in1(Instruction[11:7]), .out(WriteIndex), .sel(Imm_I_Type));  // open: in0
  // control_logic control_logic_1: pin names not known
  regfile regfile_1 (
    .ReadIndex1(ReadIndex1), .WriteIndex(WriteIndex), .WriteData(ALU_RES), .RegWEn(1'b1), .clk(clk), .ra(ra),
    .sp(sp), .t0(t0), .t1(t1), .t2(t2), .s0(s0), .s1(s1), .a0(a0), .ReadData1(ALU_A),
    .ReadData2(regfile_1_readdata2));  // open: ReadIndex2
  imm_gen imm_gen_1 (.Instruction(Instruction), .Immediate(Immediate));  // open: ImmSel
  Multiplexer #(.width(32)) multiplexer_3 (.in0(regfile_1_readdata2), .in1(Immediate), .out(ALU_B), .sel(isAddi));
  alu alu_1 (.A(ALU_A), .B(ALU_B), .ALUSel(4'b0000), .ALUResult(ALU_RES));
  // branch_comp branch_comp_1: pin names not known
  // partial_store partial_store_1: pin names not known
  // partial_load partial_load_1: pin names not known

  assign I_rd = Instruction[11:7];
  assign I_rs1 = Instruction[19:15];

  // Other names for the same wires on the sheet: Opcode[6:0] = Instruction[6:0];
  //   Instruction31_7[24:0] = Instruction[31:7]; I_funct3[2:0] = Instruction[14:12]; WriteData[31:0] = ALU_RES

  // Notes on the sheet:
  //   To IMEM
  //   IMEM (do **NOT** move this)
  //   From IMEM
  //   Inputs/Outputs for testing. Do **NOT** move these.
  //   It is OK to move the PC, RegFile, ALU, MEM, Branch Comp, Imm Gen, Partial Load, Partial Store and Control Logic to wherever is most convenient for you when constructing your CPU, and to delete this text
  //   To DMEM
  //   DMEM (do **NOT** move this)
  //   From DMEM
endmodule
